// Logisim project PuertoEntrada.circ as structural Verilog: 1 circuit, main circuit main
module main (
  input  [31:0] in_1,
  input  [15:0] in_2,
  input  _0___Read,
  output [31:0] out_4
);

  wire nand_1_out, nand_2_out, not_1_out, not_2_out, not_3_out, not_4_out, not_5_out;

  not not_1 (not_1_out, in_2[5]);
  not not_2 (not_2_out, in_2[8]);
  not not_3 (not_3_out, in_2[10]);
  not not_4 (not_4_out, in_2[13]);
  nand nand_1 (nand_1_out, ~in_2[0], ~in_2[1], ~in_2[2], ~in_2[3], ~in_2[4], ~not_1_out, ~in_2[6], ~in_2[7], ~not_2_out, ~in_2[9], ~not_3_out, ~in_2[11], ~in_2[12], ~not_4_out, ~in_2[14], ~in_2[15]);  // NAND_Gate
  nand nand_2 (nand_2_out, ~nand_1_out, ~_0___Read);  // NAND_Gate
  not not_5 (not_5_out, nand_2_out);
  assign out_4 = not_5_out ? in_1 : 32'bz;  // Controlled_Buffer controlled_buffer_1

  // Notes on the sheet:
  //   Bus Direcciones
  //   Bus Control
  //   1 - floated
  //   Puerto de Entrada
  //   Bus de Datos
  //   Puerto 2520H
endmodule
