// Logisim project 32bALU.circ as structural Verilog: 3 circuits, main circuit 32bALU
module _32bALU (
  input  [31:0] A,
  input  [3:0] Funcion,
  input  [31:0] B,
  input  Cin,
  output [31:0] Resultado,
  output Zero,
  output Ov,
  output Cout
);

  wire adder_1_cout, adder_2_cout, adder_3_cout, subtractor_1_bout, subtractor_2_bout;
  wire [31:0] adder_1_out, adder_2_out, adder_3_out, and_1_out, not_1_out, or_1_out, shifter_1_out,
       shifter_2_out, shifter_3_out, shifter_4_out, subtractor_1_out, subtractor_2_out, subtractor_3_out,
       xor_1_out;

  assign and_1_out = A & B;  // AND_Gate and_1, 32 bits wide
  assign or_1_out = A | B;  // OR_Gate or_1, 32 bits wide
  assign xor_1_out = A ^ B;  // XOR_Gate xor_1, 32 bits wide
  assign not_1_out = ~A;  // NOT_Gate not_1, 32 bits wide
  Adder #(.width(32)) adder_1 (.a(A), .b(B), .out(adder_1_out), .cout(adder_1_cout));  // open: cin
  Adder #(.width(32)) adder_2 (.a(A), .b(B), .out(adder_2_out), .cin(Cin), .cout(adder_2_cout));
  Subtractor #(.width(32)) subtractor_1 (.a(B), .b(A), .out(subtractor_1_out), .bout(subtractor_1_bout));  // open: bin
  Subtractor #(.width(32)) subtractor_2 (.a(B), .b(A), .out(subtractor_2_out), .bin(Cin), .bout(subtractor_2_bout));
  Adder #(.width(32)) adder_3 (.a(A), .b(32'h1), .out(adder_3_out), .cout(adder_3_cout));  // open: cin
  Subtractor #(.width(32)) subtractor_3 (.a(A), .b(32'h1), .out(subtractor_3_out));  // open: bin, bout
  Shifter #(.width(32)) shifter_1 (.in(A), .\dist (5'b00001), .out(shifter_1_out));
  Shifter #(.width(32), .shift("lr")) shifter_2 (.in(A), .\dist (5'b00001), .out(shifter_2_out));
  Shifter #(.width(32), .shift("rl")) shifter_3 (.in(A), .\dist (5'b00001), .out(shifter_3_out));
  Shifter #(.width(32), .shift("rr")) shifter_4 (.in(A), .\dist (5'b00001), .out(shifter_4_out));
  Multiplexer #(.select(4), .width(32), .enable("false")) multiplexer_1 (
    .in1(and_1_out), .in2(or_1_out), .in3(xor_1_out), .in4(not_1_out), .in5(adder_1_out), .in6(adder_2_out),
    .in7(subtractor_1_out), .in8(subtractor_2_out), .in9(adder_3_out), .in10(subtractor_3_out),
    .in11(shifter_1_out), .in12(shifter_2_out), .in13(shifter_3_out), .in14(shifter_4_out), .out(Resultado),
    .sel(Funcion));  // open: in0, in15
  mux mux_1 (
    .out_6(Cout), .in_1(adder_1_cout), .in_2(adder_2_cout), .in_3(subtractor_1_bout),
    .in_4(subtractor_2_bout), .in_5(Funcion));
  Comparator #(.width(32)) comparator_1 (.a(Resultado), .b({32{1'b0}}), .eq(Zero));  // open: gt, lt
  Comparator #(.width(32), .mode("unsigned")) comparator_2 (.a(Resultado), .b({32{1'b1}}), .gt(Ov));  // open: eq, lt

  // Notes on the sheet:
  //   bits
  //   3210
  //   ALU 32 bits
  //   Tabla de funciones
  //   0000 Nada
  //   0001 AND A,B
  //   0010 OR A,B
  //   0011 XOR A,B
  //   0100 NOT A
  //   0101 ADD A,B
  //   0110 ADC A,B
  //   0111 SUB B,A
  //   1000 SBB B,A
  //   1001 INC A
  //   1010 DEC A
  //   1011 SHL A
  //   1100 SHR A
  //   1101 ROL A
  //   1110 ROR A
endmodule

module Main (
  input  [7:0] in_1,
  input  [7:0] in_2,
  input  [3:0] in_3,
  input  in_4,
  output [7:0] out_5,
  output out_6,
  output out_7,
  output out_8
);

  // _32bALU 32balu_1: pin names not known; wires that end beside it: in_1, in_2, in_3, in_4, out_5, out_6, out_7, out_8

  // Notes on the sheet:
  //   Tabla de funciones
  //   0000 Nada
  //   0001 AND A,B
  //   0010 OR A,B
  //   0011 XOR A,B
  //   0100 NOT A
  //   0101 ADD A,B
  //   0110 ADC A,B
  //   0111 SUB B,A
  //   1000 SBB B,A
  //   1001 INC A
  //   1010 DEC A
  //   1011 SHL A
  //   1100 SHR A
  //   1101 ROL A
  //   1110 ROR A
endmodule

module mux (
  input  in_1,
  input  in_2,
  input  in_3,
  input  in_4,
  input  [3:0] in_5,
  output out_6
);

  wire and_1_out, and_2_out, and_3_out, and_4_out;

  and and_1 (and_1_out, in_1, ~in_5[3], in_5[2], ~in_5[1], in_5[0]);  // AND_Gate
  or or_1 (out_6, and_1_out, and_2_out, and_3_out, and_4_out);
  and and_2 (and_2_out, in_2, ~in_5[3], in_5[2], in_5[1], ~in_5[0]);  // AND_Gate
  and and_3 (and_3_out, in_3, ~in_5[3], in_5[2], in_5[1], in_5[0]);  // AND_Gate
  and and_4 (and_4_out, in_4, in_5[3], ~in_5[2], ~in_5[1], ~in_5[0]);  // AND_Gate
endmodule
